# Fritzing sketch wiringLaserPointer (saved by Fritzing 0.9.4)
breadboards: 1

parts:
  Q1 = NPN-Transistor [package="TO92 [THT]"]
  R2 = Resistor [tolerance=±5% resistance=10k package=THT]
  R1 = Resistor [tolerance=±5% resistance=100 package=THT]
  U1 = ESP32S-HiLetgo [part_number=ESP32S-HiLetgo]
  Servo_Tilt = Basic Servo
  Servo_Pan = Basic Servo
  Laser = Round Pushbutton
  6V = Power plug
  5V_HLK-PM01 = Power plug

nets:
  N1: Q1.E, Laser.leg1
  N2: Q1.B, R2.Pin_1, R1.Pin_1
  GND: Q1.C, R2.Pin_0, Servo_Tilt.gnd, Servo_Pan.gnd, Laser.leg0, 6V.GND
  N3: R1.Pin_0, U1.GPIO4
  N4: U1.GPIO12, Servo_Tilt.pulse
  GND_2: U1.GND, 5V_HLK-PM01.GND
  N5: U1.GPIO13, Servo_Pan.pulse
  VIN: U1.VIN, 5V_HLK-PM01.VCC
  VCC: Servo_Tilt.vcc, Servo_Pan.vcc, 6V.VCC

notes:
  D12 Tilt servo
  D13 Pan servo
  D4 laser

custom parts:
  ESP32S-HiLetgo: HiLetgo ESP-WROOM-32 ESP32 ESP-32S Development Board 2.4GHz Dual-Mode WiFi + Bluetooth Dual Cores Microcontroller The ESP32 integrated with Antenna switches, RF Balun, power amplifiers, low-noise amplifiers, filters, and management modules, and the entire solution occupies the least area of PCB. 2.4 GHz Wi-Fi plus Bluetooth dual-mode chip, with TSMC Ultra-low power consumption 40nm technology,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
